// Logisim project 14.circ as structural Verilog: 1 circuit, main circuit main
module main (
  input  in_1,
  input  in_2,
  input  in_3,
  output out_4
);

  wire and_1_out, not_1_out, not_2_out, not_3_out, not_4_out, or_1_out, or_2_out, or_3_out;

  not not_1 (not_1_out, in_1);
  not not_2 (not_2_out, in_2);
  or or_1 (or_1_out, not_1_out, in_2);
  or or_2 (or_2_out, not_2_out, in_3);
  not not_3 (not_3_out, in_1);
  or or_3 (or_3_out, not_3_out, in_3);
  and and_1 (and_1_out, or_1_out, or_2_out);
  not not_4 (not_4_out, and_1_out);
  or or_4 (out_4, not_4_out, or_3_out);
endmodule
