// Logisim project 15.circ as structural Verilog: 1 circuit, main circuit main
module main (
  input  A,
  input  B,
  input  C,
  input  D,
  output out_5
);

  wire and_1_out, not_1_out, not_2_out, xor_1_out;

  not not_1 (not_1_out, A);
  xor xor_1 (xor_1_out, not_1_out, B);
  and and_1 (and_1_out, C, D);
  not not_2 (not_2_out, xor_1_out);
  or or_1 (out_5, not_2_out, and_1_out);
endmodule
