// Logisim project 16.circ as structural Verilog: 1 circuit, main circuit main
module main (
  input  A,
  input  B,
  input  C,
  input  D,
  output out_5
);

  wire and_1_out, and_2_out, not_1_out, or_1_out, xnor_1_out;

  and and_1 (and_1_out, A, C);
  or or_1 (or_1_out, C, D);
  xnor xnor_1 (xnor_1_out, A, B);
  and and_2 (and_2_out, xnor_1_out, and_1_out, or_1_out);
  not not_1 (not_1_out, and_2_out);
  or or_2 (out_5, not_1_out, D);
endmodule
