// Logisim project 5.circ as structural Verilog: 1 circuit, main circuit main
module main (
  input  in_1,
  input  in_2,
  output out_3
);

  wire xor_1_out;

  xor xor_1 (xor_1_out, in_1, in_2);
  not not_1 (out_3, xor_1_out);
endmodule
